// Logisim project 4_.circ as structural Verilog: 1 circuit, main circuit main
module main (
  input  B,
  input  A,
  input  CarryIn,
  input  [2:0] Operation,
  input  Binvert,
  input  in_6,
  output Result,
  output out_8
);

  wire adder_1_out, and_1_out, multiplexer_1_out, multiplexer_2_out, not_1_out, not_2_out, or_1_out;

  not not_1 (not_1_out, B);
  not not_2 (not_2_out, A);
  Multiplexer multiplexer_1 (.in0(not_2_out), .in1(A), .out(multiplexer_1_out), .sel(in_6));
  Multiplexer multiplexer_2 (.in0(not_1_out), .in1(B), .out(multiplexer_2_out), .sel(Binvert));
  and and_1 (and_1_out, multiplexer_1_out, multiplexer_2_out);
  or or_1 (or_1_out, multiplexer_1_out, multiplexer_2_out);
  Adder #(.width(1)) adder_1 (
    .a(multiplexer_1_out), .b(multiplexer_2_out), .out(adder_1_out), .cin(CarryIn), .cout(out_8));
  Multiplexer #(.select(3)) multiplexer_3 (
    .in3(and_1_out), .in5(or_1_out), .in7(adder_1_out), .out(Result), .sel(Operation));  // open: in0, in1, in2, in4, in6

  // Notes on the sheet:
  //   Ainvert
  //   CarryOut
endmodule
